# Fritzing sketch Toggle_LED_GPIO_J4_pin_40_P43_3_fritzing (saved by Fritzing 0.9.10b)
breadboards: 1

parts:
  Mod1 = Raspberry Pi 4B
  LED1 = smd LED [color="Red (633nm)" package="1206 [SMD]"]
  R1 = Resistor [tolerance=±5% resistance=330 package="2512 [SMD]"]

nets:
  N1: Mod1.5V, LED1.cathode
  N2: Mod1.GPIO21, R1.Pin_1
  N3: LED1.anode, R1.Pin_0
